# Fritzing sketch smart-plant-monitoring-irrigation-system (saved by Fritzing 0.9.3b)
breadboards: 2

parts:
  U1 = NodeMCU V1.0
  BATT1 = 4xAA Switchable Battery Pack w/JST connector
  KY-1 = Keyes Relay [package=THT]
  WATER_PUMP1 = water pump/motor  # not connected
  J2 = male pin header, 3 pins [form="♂ (male)"]
  부품3 = FC-28 Soil Hygrometer Module - Probe
  부품4 = FC-28 Soil Hygrometer Module
  Water_Level_Sensor1 = Water Level Sensor
  MUX1 = 74HC4051 [package="DIP (Dual Inline) [THT]"]
  Squix1 = OLED 0.96" 128x64 I2C SSD1306

nets:
  N1: U1.D1, Squix1.SCL
  N2: U1.D2, Squix1.SCA
  N3: U1.D3, KY-1.signal
  N4: U1.D4, J2.pin2
  VCC: U1.3V3, J2.pin1, 부품4.VCC, Water_Level_Sensor1.VCC, MUX1.VDD, Squix1.VCC
  GND: U1.GND, KY-1.ground, J2.pin3, 부품4.GND, Water_Level_Sensor1.GND, MUX1.INH, MUX1.VEE, MUX1.VSS, Squix1.GND
  N5: U1.D5, MUX1.C, MUX1.B, MUX1.A
  N6: U1.Vin, KY-1.power
  N7: U1.A0, MUX1.IO
  N8: BATT1.POS, KY-1.C
  N9: 부품3.POS, 부품4.POS
  N10: 부품3.NEG, 부품4.NEG
  N11: 부품4.AO, MUX1.IO0
  N12: Water_Level_Sensor1.SIG, MUX1.IO7

custom parts:
  NodeMCU V1.0: ESP8266 based NodeMCU
  4xAA Switchable Battery Pack w/JST connector: 4xAA Switchable Battery Pack with JST connector
  Keyes Relay: The Keyes 5V relay module is suitable for SCM development, home appliance control. It uses a 5V~12V TIL control signal which can control DC / AC signal.
  water pump/motor: WATER PUMP BY ARDUBLOCKTR
  FC-28 Soil Hygrometer Module - Probe: The FC-28 is a soil hygrometer module that uses the Texas Instruments LM393 comparator chip to provide an analog measurement of soil humidity.
  FC-28 Soil Hygrometer Module: The FC-28 is a soil hygrometer module that uses the Texas Instruments LM393 comparator chip to provide an analog measurement of soil humidity. The digital output is high when soil moisture is over a certain threshold, as determined by adjusting the potentiometer.
  Water Level Sensor: A water level sensor. This sensor operates at 3V to 5V. The Sig (signal) pin outputs an analogue signal that is in proportion to the amount of water in contact with the sensor.
  74HC4051: 8 channel analog multiplexer/demultiplexer
